# Fritzing sketch Sensor Temperatura (saved by Fritzing 0.8.7b)
breadboards: 1

parts:
  Componente1 = Arduino Uno (Rev3)
  T1 = DS18B20 Temperature Sensor [part_number=DS18B20 package="TO92 [THT]"]
  RHT1 = Humidity and Temperature Sensor RHT03
  R1 = Resistor [tolerance=±5% resistance=10 package=THT]
  R2 = Resistor [tolerance=±5% resistance=4.7 package=THT]

nets:
  N1: Componente1.D10_PWM/SS, T1.DQ, R2.Pin_1
  N2: Componente1.D2, RHT1.Data-signal, R1.Pin_0
  5V: Componente1.5V, T1.+Vdd, RHT1.Vcc, R1.Pin_1, R2.Pin_0
  GND: Componente1.GND, T1.GND, RHT1.GND_1

custom parts:
  DS18B20 Temperature Sensor: A DS18B20 temperature sensor
