# Fritzing sketch Sensor Turbidez 2 (saved by Fritzing 0.8.7b)
breadboards: 1

parts:
  Componente1 = Arduino Uno (Rev3)
  IR1 = TSOP312.., 314.. [package=THT]
  LED1 = LED - 3mm [color="Red (633nm)" package="3 mm [THT]"]
  R1 = Resistor [tolerance=±5% resistance=220 package=THT]

nets:
  N1: Componente1.D13/SCK, R1.Pin_1
  N2: Componente1.D2, IR1.Data
  N3: Componente1.5V, IR1.Vs
  GND: Componente1.GND, IR1.GND, LED1.cathode
  N4: LED1.anode, R1.Pin_0
