# Fritzing sketch Sensor Temperatura (saved by Fritzing 0.8.7b)
circuit board: 8.46667cm x 5.64444cm
breadboards: 1

parts:
  Componente1 = Arduino Uno (Rev3)
  DS18B20 = DS18B20 Temperature Sensor [part_number=DS18B20 package="TO92 [THT]"]
  DHT11 = Humidity and Temperature Sensor RHT03
  R1 = Resistor [tolerance=±5% resistance=10 package=THT]
  R2 = Resistor [tolerance=±5% resistance=4.7 package=THT]

nets:
  N1: Componente1.D10_PWM/SS, DS18B20.DQ, R2.Pin_1
  GND: Componente1.GND, DS18B20.GND, DHT11.GND_1
  N2: Componente1.D2, DHT11.Data-signal, R1.Pin_0
  5V: Componente1.5V, DS18B20.+Vdd, DHT11.Vcc, R1.Pin_1, R2.Pin_0

custom parts:
  DS18B20 Temperature Sensor: A DS18B20 temperature sensor
