# Fritzing sketch Sensor Turbidez (saved by Fritzing 0.8.7b)
circuit board: 8.46667cm x 5.64444cm
breadboards: 1

parts:
  Componente1 = Arduino Uno (Rev3)
  IR_Rx = TSOP312.., 314.. [package=THT]
  IR_Tx = LED - 3mm [color="Infrared (940nm)" package="3 mm [THT]"]
  R1 = Resistor [tolerance=±5% resistance=220 package=THT]

nets:
  N1: Componente1.D2, IR_Rx.Data
  N2: Componente1.D4, R1.Pin_1
  N3: Componente1.5V, IR_Rx.Vs
  GND: Componente1.GND, IR_Rx.GND, IR_Tx.cathode
  N4: IR_Tx.anode, R1.Pin_0
